// Logisim project xor.circ as structural Verilog: 1 circuit, main circuit main
module main (
  input  x,
  input  y,
  output x_XOR_y
);

  wire and_1_out, and_2_out, not_1_out, not_2_out;

  not not_1 (not_1_out, x);
  not not_2 (not_2_out, y);
  and and_1 (and_1_out, not_1_out, y);
  and and_2 (and_2_out, x, not_2_out);
  or or_1 (x_XOR_y, and_1_out, and_2_out);

  // Notes on the sheet:
  //   x          y        x XOR y
  //   0          0        0
  //   1          0        1
  //   0          1        1
  //   1          1        0
  //   异或门
endmodule
